// Logisim project ISA_12_Bit.circ as structural Verilog: 13 circuits, main circuit main
module main (
  input  Clock,
  output Cout
);

  wire alu_design_1_zero, and_1_out, Bin, bne_pin, Branch, branch_pin, Cin, default_reg, dr_ac, I_pin, jump,
       Load_Pin, LW_EN, N_F, not_1_out, Reg_WE, sll_p, slt, SW_EN, Zero_Signal;
  wire [2:0] ALU_OP;
  wire [3:0] multiplexer_1_out;
  wire [11:0] adder_1_out, adder_2_out, adder_3_out, bit_extender_1_out, bit_extender_3_out,
       multiplexer_2_out, multiplexer_7_out, register_1_q, rom_1_data;
  wire [15:0] alu_design_1_alu_result, bit_extender_2_out, bit_extender_4_out, multiplexer_3_out,
       multiplexer_4_out, multiplexer_5_out, multiplexer_6_out, multiplexer_8_out, multiplexer_9_out,
       ram_1_dout, register_file_1_read_data_1, register_file_1_read_data_2, register_file_1_t0, shift_left;

  Adder #(.width(12)) adder_1 (.a(register_1_q), .b(12'h1), .out(adder_1_out));  // open: cin, cout
  Register #(.width(12)) register_1 (.D(multiplexer_7_out), .en(Clock), .Q(register_1_q), .clk(Clock));  // open: clr
  ROM #(.addrWidth(12), .dataWidth(12)) rom_1 (.addr(register_1_q), .data(rom_1_data));
  Adder #(.width(12)) adder_2 (.a(adder_1_out), .b(bit_extender_1_out), .out(adder_2_out));  // open: cin, cout
  Control_New control_new_1 (
    .OP_Code(rom_1_data[11:8]), .Bin(Bin), .Cin(Cin), .Reg_WE(Reg_WE), .default_reg(default_reg),
    .Zero_C(Zero_Signal), .Load_Pin(Load_Pin), .LE(LW_EN), .SE(SW_EN), .bne(bne_pin),
    .Branch_Pin(branch_pin), .Jump(jump), .Slt_pin(slt), .sll_pin(sll_p), .dr_ac(dr_ac), .I_pin(I_pin),
    .ALU_OP(ALU_OP));
  Multiplexer #(.width(4)) multiplexer_1 (.in0(rom_1_data[7:4]), .in1(4'b1000), .out(multiplexer_1_out), .sel(dr_ac));
  Multiplexer #(.width(12)) multiplexer_2 (.in0(adder_1_out), .in1(adder_2_out), .out(multiplexer_2_out), .sel(Branch));
  Register_File register_file_1 (
    .RD(multiplexer_1_out), .Input_Data(multiplexer_3_out), .Reg_Write_EN(Reg_WE), .Clock(Clock),
    .Read_Reg_2(rom_1_data[7:4]), .Read_Reg_1(rom_1_data[3:0]), .t0(register_file_1_t0),
    .Read_Data_1(register_file_1_read_data_1), .Read_Data_2(register_file_1_read_data_2));
  Multiplexer #(.width(16)) multiplexer_3 (
    .in0(multiplexer_6_out), .in1(bit_extender_2_out), .out(multiplexer_3_out), .sel(slt));
  assign bit_extender_1_out = {{8{1'b0}}, rom_1_data[3:0]};  // Bit_Extender bit_extender_1
  assign bit_extender_2_out = {{15{1'b0}}, N_F};  // Bit_Extender bit_extender_2
  assign bit_extender_3_out = {{4{rom_1_data[7]}}, rom_1_data[7:0]};  // Bit_Extender bit_extender_3
  assign bit_extender_4_out = {{12{1'b0}}, rom_1_data[3:0]};  // Bit_Extender bit_extender_4
  Multiplexer #(.width(16)) multiplexer_4 (
    .in0(register_file_1_read_data_1), .in1(bit_extender_4_out), .out(multiplexer_4_out), .sel(I_pin));
  Multiplexer #(.width(16)) multiplexer_5 (
    .in0(register_file_1_read_data_2), .in1(register_file_1_t0), .out(multiplexer_5_out), .sel(default_reg));
  Multiplexer #(.width(16)) multiplexer_6 (
    .in0(multiplexer_9_out), .in1(shift_left), .out(multiplexer_6_out), .sel(sll_p));
  RAM #(.addrWidth(16), .asyncread("true"), .dataWidth(16)) ram_1 (
    .addr(alu_design_1_alu_result), .we(SW_EN), .oe(LW_EN), .clk(Clock), .din(register_file_1_read_data_2),
    .dout(ram_1_dout));
  Multiplexer #(.width(12)) multiplexer_7 (
    .in0(multiplexer_2_out), .in1(adder_3_out), .out(multiplexer_7_out), .sel(jump));
  Adder #(.width(12)) adder_3 (.a(multiplexer_2_out), .b(bit_extender_3_out), .out(adder_3_out));  // open: cin, cout
  Shifter #(.width(16)) shifter_1 (.in(register_file_1_read_data_2), .\dist (rom_1_data[3:0]), .out(shift_left));
  Multiplexer #(.width(16)) multiplexer_8 (
    .in0(multiplexer_4_out), .in1(register_file_1_read_data_2), .out(multiplexer_8_out), .sel(branch_pin));
  ALU_Design alu_design_1 (
    .Data_1(multiplexer_5_out), .Data_2(multiplexer_8_out), .ALU_OPcode(ALU_OP), .Invert(Bin), .Cin(Cin),
    .ALU_Result(alu_design_1_alu_result), .ZerO(alu_design_1_zero), .Cout(Cout), .N_F(N_F));
  Multiplexer #(.width(16)) multiplexer_9 (
    .in0(alu_design_1_alu_result), .in1(ram_1_dout), .out(multiplexer_9_out), .sel(Load_Pin));
  and and_1 (and_1_out, alu_design_1_zero, Zero_Signal);
  Multiplexer multiplexer_10 (.in0(and_1_out), .in1(not_1_out), .out(Branch), .sel(bne_pin));
  not not_1 (not_1_out, alu_design_1_zero);

  // Other names for the same wires on the sheet: Mem_Clk = Clock

  // Notes on the sheet:
  //   contents of rom_1 (hex, n*v repeats v):
  //   2f1 410 f16 512 745 932 a31 f16 0 0 c23 ff2 0 0 d34 e67 f14 8*0 ff1 6*0 f10 4*0 f05 11*0 f1 4044*0
  //   ff1
endmodule

module Register_File (
  input  [15:0] Input_Data,
  input  [3:0] Read_Reg_1,
  input  [3:0] RD,
  input  [3:0] Read_Reg_2,
  input  Clock,
  input  Reg_Write_EN,
  output [15:0] Read_Data_1,
  output [15:0] Read_Data_2,
  output [15:0] t0
);

  wire and_1_out, and_2_out, and_3_out, and_4_out, and_5_out, and_6_out, and_7_out, and_8_out, and_9_out,
       and_10_out, and_11_out, and_12_out, and_13_out, and_14_out, and_15_out, and_16_out, decoder_1_out0,
       decoder_1_out1, decoder_1_out2, decoder_1_out3, decoder_1_out4, decoder_1_out5, decoder_1_out6,
       decoder_1_out7, decoder_1_out8, decoder_1_out9, decoder_1_out10, decoder_1_out11, decoder_1_out12,
       decoder_1_out13, decoder_1_out14, decoder_1_out15;
  wire [15:0] R0_q, R1_q, R2_q, R3_q, R4_q, R5_q, R6_q, R7_q, R9_q, R10_q, R11_q, R12_q, R13_q, R14_q, R15_q;

  Decoder #(.select(4)) decoder_1 (
    .out0(decoder_1_out0), .out1(decoder_1_out1), .out2(decoder_1_out2), .out3(decoder_1_out3),
    .out4(decoder_1_out4), .out5(decoder_1_out5), .out6(decoder_1_out6), .out7(decoder_1_out7),
    .out8(decoder_1_out8), .out9(decoder_1_out9), .out10(decoder_1_out10), .out11(decoder_1_out11),
    .out12(decoder_1_out12), .out13(decoder_1_out13), .out14(decoder_1_out14), .out15(decoder_1_out15),
    .sel(RD));  // open: en
  and and_1 (and_1_out, decoder_1_out0, Reg_Write_EN);
  and and_2 (and_2_out, decoder_1_out1, Reg_Write_EN);
  and and_3 (and_3_out, decoder_1_out2, Reg_Write_EN);
  and and_4 (and_4_out, decoder_1_out3, Reg_Write_EN);
  and and_5 (and_5_out, decoder_1_out4, Reg_Write_EN);
  and and_6 (and_6_out, decoder_1_out5, Reg_Write_EN);
  and and_7 (and_7_out, decoder_1_out6, Reg_Write_EN);
  and and_8 (and_8_out, decoder_1_out7, Reg_Write_EN);
  and and_9 (and_9_out, decoder_1_out8, Reg_Write_EN);
  and and_10 (and_10_out, decoder_1_out9, Reg_Write_EN);
  and and_11 (and_11_out, decoder_1_out10, Reg_Write_EN);
  and and_12 (and_12_out, decoder_1_out11, Reg_Write_EN);
  and and_13 (and_13_out, decoder_1_out12, Reg_Write_EN);
  and and_14 (and_14_out, decoder_1_out13, Reg_Write_EN);
  and and_15 (and_15_out, decoder_1_out14, Reg_Write_EN);
  and and_16 (and_16_out, decoder_1_out15, Reg_Write_EN);
  Register #(.width(16)) R0 (.D({16{1'b0}}), .en(and_1_out), .Q(R0_q), .clk(Clock));  // open: clr
  Register #(.width(16)) R1 (.D(Input_Data), .en(and_2_out), .Q(R1_q), .clk(Clock));  // open: clr
  Register #(.width(16)) R2 (.D(Input_Data), .en(and_3_out), .Q(R2_q), .clk(Clock));  // open: clr
  Register #(.width(16)) R3 (.D(Input_Data), .en(and_4_out), .Q(R3_q), .clk(Clock));  // open: clr
  Register #(.width(16)) R4 (.D(Input_Data), .en(and_5_out), .Q(R4_q), .clk(Clock));  // open: clr
  Register #(.width(16)) R5 (.D(Input_Data), .en(and_6_out), .Q(R5_q), .clk(Clock));  // open: clr
  Register #(.width(16)) R6 (.D(Input_Data), .en(and_7_out), .Q(R6_q), .clk(Clock));  // open: clr
  Register #(.width(16)) R7 (.D(Input_Data), .en(and_8_out), .Q(R7_q), .clk(Clock));  // open: clr
  Register #(.width(16)) R8 (.D(Input_Data), .en(and_9_out), .Q(t0), .clk(Clock));  // open: clr
  Register #(.width(16)) R9 (.D(Input_Data), .en(and_10_out), .Q(R9_q), .clk(Clock));  // open: clr
  Register #(.width(16)) R10 (.D(Input_Data), .en(and_11_out), .Q(R10_q), .clk(Clock));  // open: clr
  Register #(.width(16)) R11 (.D(Input_Data), .en(and_12_out), .Q(R11_q), .clk(Clock));  // open: clr
  Register #(.width(16)) R12 (.D(Input_Data), .en(and_13_out), .Q(R12_q), .clk(Clock));  // open: clr
  Register #(.width(16)) R13 (.D(Input_Data), .en(and_14_out), .Q(R13_q), .clk(Clock));  // open: clr
  Register #(.width(16)) R14 (.D(Input_Data), .en(and_15_out), .Q(R14_q), .clk(Clock));  // open: clr
  Register #(.width(16)) R15 (.D(Input_Data), .en(and_16_out), .Q(R15_q), .clk(Clock));  // open: clr
  Multiplexer #(.select(4), .width(16)) multiplexer_1 (
    .in0(R0_q), .in1(R1_q), .in2(R2_q), .in3(R3_q), .in4(R4_q), .in5(R5_q), .in6(R6_q), .in7(R7_q), .in8(t0),
    .in9(R9_q), .in10(R10_q), .in11(R11_q), .in12(R12_q), .in13(R13_q), .in14(R14_q), .in15(R15_q),
    .out(Read_Data_1), .sel(Read_Reg_1));
  Multiplexer #(.select(4), .width(16)) multiplexer_2 (
    .in0(R0_q), .in1(R1_q), .in2(R2_q), .in3(R3_q), .in4(R4_q), .in5(R5_q), .in6(R6_q), .in7(R7_q), .in8(t0),
    .in9(R9_q), .in10(R10_q), .in11(R11_q), .in12(R12_q), .in13(R13_q), .in14(R14_q), .in15(R15_q),
    .out(Read_Data_2), .sel(Read_Reg_2));
endmodule

module ALU_Design (
  input  [2:0] ALU_OPcode,
  input  Invert,
  input  Cin,
  input  [15:0] Data_1,
  input  [15:0] Data_2,
  output ZerO,
  output [15:0] ALU_Result,
  output N_F,
  output Cout
);

  wire alu_1_bit_1_cout, alu_1_bit_2_cout, alu_1_bit_3_cout, alu_1_bit_4_cout, alu_1_bit_5_cout,
       alu_1_bit_6_cout, alu_1_bit_7_cout, alu_1_bit_8_cout, alu_1_bit_9_cout, alu_1_bit_10_cout,
       alu_1_bit_11_cout, alu_1_bit_12_cout, alu_1_bit_13_cout, alu_1_bit_14_cout, alu_1_bit_15_cout,
       or_1_out;

  ALU_1_BIT alu_1_bit_1 (
    .Input_D2(Data_2[0]), .Bin(Invert), .Cin(Cin), .Input_D1(Data_1[0]), .ALU_OPCode(ALU_OPcode),
    .Cout(alu_1_bit_1_cout), .ALU_Result(ALU_Result[0]));
  ALU_1_BIT alu_1_bit_2 (
    .Input_D2(Data_2[1]), .Bin(Invert), .Cin(alu_1_bit_1_cout), .Input_D1(Data_1[1]),
    .ALU_OPCode(ALU_OPcode), .Cout(alu_1_bit_2_cout), .ALU_Result(ALU_Result[1]));
  ALU_1_BIT alu_1_bit_3 (
    .Input_D2(Data_2[2]), .Bin(Invert), .Cin(alu_1_bit_2_cout), .Input_D1(Data_1[2]),
    .ALU_OPCode(ALU_OPcode), .Cout(alu_1_bit_3_cout), .ALU_Result(ALU_Result[2]));
  ALU_1_BIT alu_1_bit_4 (
    .Input_D2(Data_2[3]), .Bin(Invert), .Cin(alu_1_bit_3_cout), .Input_D1(Data_1[3]),
    .ALU_OPCode(ALU_OPcode), .Cout(alu_1_bit_4_cout), .ALU_Result(ALU_Result[3]));
  ALU_1_BIT alu_1_bit_5 (
    .Input_D2(Data_2[4]), .Bin(Invert), .Cin(alu_1_bit_4_cout), .Input_D1(Data_1[4]),
    .ALU_OPCode(ALU_OPcode), .Cout(alu_1_bit_5_cout), .ALU_Result(ALU_Result[4]));
  ALU_1_BIT alu_1_bit_6 (
    .Input_D2(Data_2[5]), .Bin(Invert), .Cin(alu_1_bit_5_cout), .Input_D1(Data_1[5]),
    .ALU_OPCode(ALU_OPcode), .Cout(alu_1_bit_6_cout), .ALU_Result(ALU_Result[5]));
  ALU_1_BIT alu_1_bit_7 (
    .Input_D2(Data_2[6]), .Bin(Invert), .Cin(alu_1_bit_6_cout), .Input_D1(Data_1[6]),
    .ALU_OPCode(ALU_OPcode), .Cout(alu_1_bit_7_cout), .ALU_Result(ALU_Result[6]));
  ALU_1_BIT alu_1_bit_8 (
    .Input_D2(Data_2[7]), .Bin(Invert), .Cin(alu_1_bit_7_cout), .Input_D1(Data_1[7]),
    .ALU_OPCode(ALU_OPcode), .Cout(alu_1_bit_8_cout), .ALU_Result(ALU_Result[7]));
  ALU_1_BIT alu_1_bit_9 (
    .Input_D2(Data_2[8]), .Bin(Invert), .Cin(alu_1_bit_8_cout), .Input_D1(Data_1[8]),
    .ALU_OPCode(ALU_OPcode), .Cout(alu_1_bit_9_cout), .ALU_Result(ALU_Result[8]));
  ALU_1_BIT alu_1_bit_10 (
    .Input_D2(Data_2[9]), .Bin(Invert), .Cin(alu_1_bit_9_cout), .Input_D1(Data_1[9]),
    .ALU_OPCode(ALU_OPcode), .Cout(alu_1_bit_10_cout), .ALU_Result(ALU_Result[9]));
  ALU_1_BIT alu_1_bit_11 (
    .Input_D2(Data_2[10]), .Bin(Invert), .Cin(alu_1_bit_10_cout), .Input_D1(Data_1[10]),
    .ALU_OPCode(ALU_OPcode), .Cout(alu_1_bit_11_cout), .ALU_Result(ALU_Result[10]));
  ALU_1_BIT alu_1_bit_12 (
    .Input_D2(Data_2[11]), .Bin(Invert), .Cin(alu_1_bit_11_cout), .Input_D1(Data_1[11]),
    .ALU_OPCode(ALU_OPcode), .Cout(alu_1_bit_12_cout), .ALU_Result(ALU_Result[11]));
  ALU_1_BIT alu_1_bit_13 (
    .Input_D2(Data_2[12]), .Bin(Invert), .Cin(alu_1_bit_12_cout), .Input_D1(Data_1[12]),
    .ALU_OPCode(ALU_OPcode), .Cout(alu_1_bit_13_cout), .ALU_Result(ALU_Result[12]));
  ALU_1_BIT alu_1_bit_14 (
    .Input_D2(Data_2[13]), .Bin(Invert), .Cin(alu_1_bit_13_cout), .Input_D1(Data_1[13]),
    .ALU_OPCode(ALU_OPcode), .Cout(alu_1_bit_14_cout), .ALU_Result(ALU_Result[13]));
  ALU_1_BIT alu_1_bit_15 (
    .Input_D2(Data_2[14]), .Bin(Invert), .Cin(alu_1_bit_14_cout), .Input_D1(Data_1[14]),
    .ALU_OPCode(ALU_OPcode), .Cout(alu_1_bit_15_cout), .ALU_Result(ALU_Result[14]));
  ALU_1_BIT alu_1_bit_16 (
    .Input_D2(Data_2[15]), .Bin(Invert), .Cin(alu_1_bit_15_cout), .Input_D1(Data_1[15]),
    .ALU_OPCode(ALU_OPcode), .Cout(Cout), .ALU_Result(ALU_Result[15]));
  not not_1 (N_F, ALU_Result[15]);
  or or_1 (or_1_out, ALU_Result[0], ALU_Result[1], ALU_Result[2], ALU_Result[3], ALU_Result[4], ALU_Result[5], ALU_Result[6], ALU_Result[7], ALU_Result[8], ALU_Result[9], ALU_Result[10], ALU_Result[11], ALU_Result[12], ALU_Result[13], ALU_Result[14], ALU_Result[15]);
  not not_2 (ZerO, or_1_out);

  // Other names for the same wires on the sheet: AR0 = ALU_Result[0]; AR1 = ALU_Result[1]; AR2 = ALU_Result[2];
  //   AR3 = ALU_Result[3]; AR4 = ALU_Result[4]; AR5 = ALU_Result[5]; AR6 = ALU_Result[6]; AR7 = ALU_Result[7];
  //   AR8 = ALU_Result[8]; AR9 = ALU_Result[9]; AR10 = ALU_Result[10]; AR11 = ALU_Result[11]; AR12 = ALU_Result[12];
  //   AR13 = ALU_Result[13]; AR14 = ALU_Result[14]; AR15 = ALU_Result[15]; A0 = Data_1[0]; A1 = Data_1[1];
  //   A2 = Data_1[2]; A3 = Data_1[3]; A4 = Data_1[4]; A5 = Data_1[5]; A6 = Data_1[6]; A7 = Data_1[7]; A8 = Data_1[8];
  //   A9 = Data_1[9]; A10 = Data_1[10]; A11 = Data_1[11]; A12 = Data_1[12]; A13 = Data_1[13]; A14 = Data_1[14];
  //   A15 = Data_1[15]; B0 = Data_2[0]; B1 = Data_2[1]; B2 = Data_2[2]; B3 = Data_2[3]; B4 = Data_2[4];
  //   B5 = Data_2[5]; B6 = Data_2[6]; B7 = Data_2[7]; B8 = Data_2[8]; B9 = Data_2[9]; B10 = Data_2[10];
  //   B11 = Data_2[11]; B12 = Data_2[12]; B13 = Data_2[13]; B14 = Data_2[14]; B15 = Data_2[15]
endmodule

module ALU_1_BIT (
  input  Input_D1,
  input  Input_D2,
  input  Bin,
  input  Cin,
  input  [2:0] ALU_OPCode,
  output ALU_Result,
  output Cout
);

  wire adder_1_out, and_1_out, multiplexer_1_out, nand_1_out, nor_1_out, nor_2_out, not_1_out, not_2_out,
       or_1_out, xor_1_out;

  and and_1 (and_1_out, Input_D1, Input_D2);
  or or_1 (or_1_out, Input_D1, Input_D2);
  nor nor_1 (nor_1_out, Input_D1, Input_D2);
  Multiplexer multiplexer_1 (.in0(Input_D2), .in1(not_1_out), .out(multiplexer_1_out), .sel(Bin));
  not not_1 (not_1_out, Input_D2);
  xor xor_1 (xor_1_out, Input_D1, Input_D2);
  nand nand_1 (nand_1_out, Input_D1, Input_D2);
  not not_2 (not_2_out, Input_D1);
  nor nor_2 (nor_2_out, Input_D1, Input_D2);
  Adder #(.width(1)) adder_1 (.a(Input_D1), .b(multiplexer_1_out), .out(adder_1_out), .cin(Cin), .cout(Cout));
  Multiplexer #(.select(3)) multiplexer_2 (
    .in0(and_1_out), .in1(or_1_out), .in2(nor_1_out), .in3(adder_1_out), .in4(xor_1_out), .in5(nand_1_out),
    .in6(not_2_out), .in7(nor_2_out), .out(ALU_Result), .sel(ALU_OPCode));
endmodule

module R_Type (
  input  B_inv,
  input  Cin,
  input  Enable,
  input  Clock,
  output Zero,
  output Cout
);

  wire [11:0] adder_1_out, register_1_q, rom_1_data;
  wire [15:0] alu_design_1_alu_result, register_file_1_read_data_1, register_file_1_read_data_2;

  Adder #(.width(12)) adder_1 (.a(register_1_q), .b(12'h1), .out(adder_1_out));  // open: cin, cout
  Register #(.width(12)) register_1 (.D(adder_1_out), .en(Enable), .Q(register_1_q), .clk(Clock));  // open: clr
  ROM #(.addrWidth(12), .dataWidth(12)) rom_1 (.addr(register_1_q), .data(rom_1_data));
  Register_File register_file_1 (
    .RD(rom_1_data[7:4]), .Input_Data(alu_design_1_alu_result), .Clock(Clock), .Read_Reg_2(rom_1_data[7:4]),
    .Read_Reg_1(rom_1_data[3:0]), .Read_Data_1(register_file_1_read_data_1),
    .Read_Data_2(register_file_1_read_data_2));  // open: Reg_Write_EN, t0
  ALU_Design alu_design_1 (
    .Data_1(register_file_1_read_data_1), .Data_2(register_file_1_read_data_2), .Invert(B_inv), .Cin(Cin),
    .ALU_Result(alu_design_1_alu_result), .ZerO(Zero), .Cout(Cout));  // open: ALU_OPcode, N_F
endmodule

module I_type (
  input  B_inv,
  input  Cin,
  input  Enable,
  input  Clock,
  output Zero,
  output Cout
);

  wire [11:0] adder_1_out, register_1_q, rom_1_data;
  wire [15:0] alu_design_1_alu_result, bit_extender_1_out, register_file_1_read_data_2;

  Adder #(.width(12)) adder_1 (.a(register_1_q), .b(12'h1), .out(adder_1_out));  // open: cin, cout
  Register #(.width(12)) register_1 (.D(adder_1_out), .en(Enable), .Q(register_1_q), .clk(Clock));  // open: clr
  ROM #(.addrWidth(12), .dataWidth(12)) rom_1 (.addr(register_1_q), .data(rom_1_data));
  assign bit_extender_1_out = {{12{rom_1_data[3]}}, rom_1_data[3:0]};  // Bit_Extender bit_extender_1
  Register_File register_file_1 (
    .RD(rom_1_data[7:4]), .Input_Data(alu_design_1_alu_result), .Clock(Clock), .Read_Reg_2(rom_1_data[7:4]),
    .Read_Data_2(register_file_1_read_data_2));  // open: Reg_Write_EN, Read_Reg_1, t0, Read_Data_1
  ALU_Design alu_design_1 (
    .Data_1(bit_extender_1_out), .Data_2(register_file_1_read_data_2), .Invert(B_inv), .Cin(Cin),
    .ALU_Result(alu_design_1_alu_result), .ZerO(Zero), .Cout(Cout));  // open: ALU_OPcode, N_F
endmodule

module lw (
  input  B_inv,
  input  Cin,
  input  [2:0] in_3,
  input  Enable,
  input  Clock,
  output Zero,
  output Cout
);

  wire [11:0] adder_1_out, register_1_q, rom_1_data;
  wire [15:0] alu_design_1_alu_result, bit_extender_1_out, ram_1_dout, register_file_1_t0;

  Adder #(.width(12)) adder_1 (.a(register_1_q), .b(12'h1), .out(adder_1_out));  // open: cin, cout
  Register #(.width(12)) register_1 (.D(adder_1_out), .en(Enable), .Q(register_1_q), .clk(Clock));  // open: clr
  ROM #(.addrWidth(12), .dataWidth(12)) rom_1 (.addr(register_1_q), .data(rom_1_data));
  assign bit_extender_1_out = {{12{rom_1_data[3]}}, rom_1_data[3:0]};  // Bit_Extender bit_extender_1
  Register_File register_file_1 (
    .RD(rom_1_data[7:4]), .Input_Data(ram_1_dout), .Reg_Write_EN(Enable), .Clock(Clock),
    .t0(register_file_1_t0));  // open: Read_Reg_2, Read_Reg_1, Read_Data_1, Read_Data_2
  ALU_Design alu_design_1 (
    .Data_1(bit_extender_1_out), .Data_2(register_file_1_t0), .ALU_OPcode(in_3), .Invert(B_inv), .Cin(Cin),
    .ALU_Result(alu_design_1_alu_result), .ZerO(Zero), .Cout(Cout));  // open: N_F
  RAM #(.addrWidth(16), .asyncread("true"), .dataWidth(16)) ram_1 (
    .addr(alu_design_1_alu_result), .oe(Enable), .clk(Clock), .dout(ram_1_dout));  // open: we, din

  // Other names for the same wires on the sheet: Lw_en = Enable; Reg_WE = Enable

  // Notes on the sheet:
  //   contents of rom_1 (hex, n*v repeats v):
  //   144
endmodule

module sw (
  input  B_inv,
  input  Cin,
  input  [2:0] in_3,
  input  Enable,
  input  Clock,
  output Zero,
  output Cout
);

  wire [11:0] adder_1_out, register_1_q, rom_1_data;
  wire [15:0] alu_design_1_alu_result, bit_extender_1_out, register_file_1_read_data_2, register_file_1_t0;

  Adder #(.width(12)) adder_1 (.a(register_1_q), .b(12'h1), .out(adder_1_out));  // open: cin, cout
  ROM #(.addrWidth(12), .dataWidth(12)) rom_1 (.addr(register_1_q), .data(rom_1_data));
  Register #(.width(12)) register_1 (.D(adder_1_out), .en(Enable), .Q(register_1_q), .clk(Clock));  // open: clr
  assign bit_extender_1_out = {{12{rom_1_data[3]}}, rom_1_data[3:0]};  // Bit_Extender bit_extender_1
  Register_File register_file_1 (
    .RD(rom_1_data[7:4]), .Reg_Write_EN(Enable), .Clock(Clock), .Read_Reg_2(rom_1_data[7:4]),
    .t0(register_file_1_t0), .Read_Data_2(register_file_1_read_data_2));  // open: Input_Data, Read_Reg_1, Read_Data_1
  RAM #(.addrWidth(16), .asyncread("true"), .dataWidth(16)) ram_1 (
    .addr(alu_design_1_alu_result), .we(Enable), .clk(Clock), .din(register_file_1_read_data_2));  // open: oe, dout
  ALU_Design alu_design_1 (
    .Data_1(bit_extender_1_out), .Data_2(register_file_1_t0), .ALU_OPcode(in_3), .Invert(B_inv), .Cin(Cin),
    .ALU_Result(alu_design_1_alu_result), .ZerO(Zero), .Cout(Cout));  // open: N_F

  // Other names for the same wires on the sheet: Lw_en = Enable; Reg_WE = Enable; S_E = Enable

  // Notes on the sheet:
  //   contents of rom_1 (hex, n*v repeats v):
  //   123
endmodule

module branch (
  input  B_inv,
  input  Cin,
  input  Enable,
  input  Clock,
  input  [2:0] ALU_OPcode,
  input  Reg_WE,
  input  I_M,
  input  D_M,
  input  Zero_P,
  input  Load_Pin,
  input  L_E,
  input  S_E,
  input  bne_pin,
  input  Branch_MP,
  output Cout
);

  wire alu_design_1_zero, and_1_out, Branch, not_1_out;
  wire [11:0] adder_1_out, adder_2_out, bit_extender_1_out, multiplexer_1_out, register_1_q, rom_1_data;
  wire [15:0] alu_design_1_alu_result, bit_extender_2_out, multiplexer_2_out, multiplexer_3_out,
       multiplexer_4_out, multiplexer_5_out, ram_1_dout, register_file_1_read_data_1,
       register_file_1_read_data_2, register_file_1_t0;

  Adder #(.width(12)) adder_1 (.a(register_1_q), .b(12'h1), .out(adder_1_out));  // open: cin, cout
  Register #(.width(12)) register_1 (.D(multiplexer_1_out), .en(Enable), .Q(register_1_q), .clk(Clock));  // open: clr
  ROM #(.addrWidth(12), .dataWidth(12)) rom_1 (.addr(register_1_q), .data(rom_1_data));
  Adder #(.width(12)) adder_2 (.a(adder_1_out), .b(bit_extender_1_out), .out(adder_2_out));  // open: cin, cout
  Multiplexer #(.width(12)) multiplexer_1 (.in0(adder_1_out), .in1(adder_2_out), .out(multiplexer_1_out), .sel(Branch));
  assign bit_extender_1_out = {{8{1'b0}}, rom_1_data[3:0]};  // Bit_Extender bit_extender_1
  Register_File register_file_1 (
    .RD(rom_1_data[7:4]), .Input_Data(multiplexer_5_out), .Reg_Write_EN(Reg_WE), .Clock(Clock),
    .Read_Reg_2(rom_1_data[7:4]), .Read_Reg_1(rom_1_data[3:0]), .t0(register_file_1_t0),
    .Read_Data_1(register_file_1_read_data_1), .Read_Data_2(register_file_1_read_data_2));
  assign bit_extender_2_out = {{12{1'b0}}, rom_1_data[3:0]};  // Bit_Extender bit_extender_2
  Multiplexer #(.width(16)) multiplexer_2 (
    .in0(register_file_1_read_data_1), .in1(bit_extender_2_out), .out(multiplexer_2_out), .sel(I_M));
  Multiplexer #(.width(16)) multiplexer_3 (
    .in0(register_file_1_read_data_2), .in1(register_file_1_t0), .out(multiplexer_3_out), .sel(D_M));
  RAM #(.addrWidth(16), .asyncread("true"), .dataWidth(16)) ram_1 (
    .addr(alu_design_1_alu_result), .we(S_E), .oe(L_E), .clk(Clock), .din(register_file_1_read_data_2),
    .dout(ram_1_dout));
  Multiplexer #(.width(16)) multiplexer_4 (
    .in0(multiplexer_2_out), .in1(register_file_1_read_data_2), .out(multiplexer_4_out), .sel(Branch_MP));
  ALU_Design alu_design_1 (
    .Data_1(multiplexer_3_out), .Data_2(multiplexer_4_out), .ALU_OPcode(ALU_OPcode), .Invert(B_inv),
    .Cin(Cin), .ALU_Result(alu_design_1_alu_result), .ZerO(alu_design_1_zero), .Cout(Cout));  // open: N_F
  Multiplexer #(.width(16)) multiplexer_5 (
    .in0(alu_design_1_alu_result), .in1(ram_1_dout), .out(multiplexer_5_out), .sel(Load_Pin));
  and and_1 (and_1_out, alu_design_1_zero, Zero_P);
  Multiplexer multiplexer_6 (.in0(and_1_out), .in1(not_1_out), .out(Branch), .sel(bne_pin));
  not not_1 (not_1_out, alu_design_1_zero);

  // Other names for the same wires on the sheet: branch_pin = Branch_MP; default_reg = D_M; I_pin = I_M; LW_EN = L_E;
  //   Mem_Clk = Clock; SW_EN = S_E; Zero_Signal = Zero_P

  // Notes on the sheet:
  //   contents of rom_1 (hex, n*v repeats v):
  //   11 5*0 6
endmodule

module jump (
  input  B_inv,
  input  Cin,
  input  Enable,
  input  Clock,
  input  [2:0] ALU_OPcode,
  input  Reg_WE,
  input  I_C,
  input  t0_C,
  input  Zero_C,
  input  Load_Pin,
  input  L_E,
  input  S_E,
  input  bne_pin,
  input  Branch_MP,
  input  Jump_pin,
  output Cout
);

  wire alu_design_1_zero, and_1_out, Branch, not_1_out;
  wire [11:0] adder_1_out, adder_2_out, adder_3_out, bit_extender_1_out, bit_extender_2_out,
       multiplexer_1_out, multiplexer_5_out, register_1_q, rom_1_data;
  wire [15:0] alu_design_1_alu_result, bit_extender_3_out, multiplexer_2_out, multiplexer_3_out,
       multiplexer_4_out, multiplexer_6_out, ram_1_dout, register_file_1_read_data_1,
       register_file_1_read_data_2, register_file_1_t0;

  Adder #(.width(12)) adder_1 (.a(register_1_q), .b(12'h1), .out(adder_1_out));  // open: cin, cout
  Register #(.width(12)) register_1 (.D(multiplexer_5_out), .en(Enable), .Q(register_1_q), .clk(Clock));  // open: clr
  ROM #(.addrWidth(12), .dataWidth(12)) rom_1 (.addr(register_1_q), .data(rom_1_data));
  Adder #(.width(12)) adder_2 (.a(adder_1_out), .b(bit_extender_1_out), .out(adder_2_out));  // open: cin, cout
  Multiplexer #(.width(12)) multiplexer_1 (.in0(adder_1_out), .in1(adder_2_out), .out(multiplexer_1_out), .sel(Branch));
  Register_File register_file_1 (
    .RD(rom_1_data[7:4]), .Input_Data(multiplexer_6_out), .Reg_Write_EN(Reg_WE), .Clock(Clock),
    .Read_Reg_2(rom_1_data[7:4]), .Read_Reg_1(rom_1_data[3:0]), .t0(register_file_1_t0),
    .Read_Data_1(register_file_1_read_data_1), .Read_Data_2(register_file_1_read_data_2));
  assign bit_extender_1_out = {{8{1'b0}}, rom_1_data[3:0]};  // Bit_Extender bit_extender_1
  assign bit_extender_2_out = {{4{1'b0}}, rom_1_data[7:0]};  // Bit_Extender bit_extender_2
  assign bit_extender_3_out = {{12{1'b0}}, rom_1_data[3:0]};  // Bit_Extender bit_extender_3
  Multiplexer #(.width(16)) multiplexer_2 (
    .in0(register_file_1_read_data_1), .in1(bit_extender_3_out), .out(multiplexer_2_out), .sel(I_C));
  Multiplexer #(.width(16)) multiplexer_3 (
    .in0(register_file_1_read_data_2), .in1(register_file_1_t0), .out(multiplexer_3_out), .sel(t0_C));
  RAM #(.addrWidth(16), .asyncread("true"), .dataWidth(16)) ram_1 (
    .addr(alu_design_1_alu_result), .we(S_E), .oe(L_E), .clk(Clock), .din(register_file_1_read_data_2),
    .dout(ram_1_dout));
  Adder #(.width(12)) adder_3 (.a(multiplexer_1_out), .b(bit_extender_2_out), .out(adder_3_out));  // open: cin, cout
  Multiplexer #(.width(16)) multiplexer_4 (
    .in0(multiplexer_2_out), .in1(register_file_1_read_data_2), .out(multiplexer_4_out), .sel(Branch_MP));
  Multiplexer #(.width(12)) multiplexer_5 (
    .in0(multiplexer_1_out), .in1(adder_3_out), .out(multiplexer_5_out), .sel(Jump_pin));
  ALU_Design alu_design_1 (
    .Data_1(multiplexer_3_out), .Data_2(multiplexer_4_out), .ALU_OPcode(ALU_OPcode), .Invert(B_inv),
    .Cin(Cin), .ALU_Result(alu_design_1_alu_result), .ZerO(alu_design_1_zero), .Cout(Cout));  // open: N_F
  Multiplexer #(.width(16)) multiplexer_6 (
    .in0(alu_design_1_alu_result), .in1(ram_1_dout), .out(multiplexer_6_out), .sel(Load_Pin));
  and and_1 (and_1_out, alu_design_1_zero, Zero_C);
  Multiplexer multiplexer_7 (.in0(and_1_out), .in1(not_1_out), .out(Branch), .sel(bne_pin));
  not not_1 (not_1_out, alu_design_1_zero);

  // Other names for the same wires on the sheet: branch_pin = Branch_MP; default_reg = t0_C; I_pin = I_C;
  //   jump = Jump_pin; LW_EN = L_E; Mem_Clk = Clock; SW_EN = S_E; Zero_Signal = Zero_C

  // Notes on the sheet:
  //   contents of rom_1 (hex, n*v repeats v):
  //   789 5*0 6
endmodule

module slt (
  input  B_inv,
  input  Cin,
  input  Enable,
  input  Clock,
  input  [2:0] ALU_OPcode,
  input  Reg_WE,
  input  I_C,
  input  t0_C,
  input  Zero_C,
  input  Load_Pin,
  input  L_E,
  input  S_E,
  input  bne_pin,
  input  Branch_MP,
  input  Jump_pin,
  input  Slt_pin,
  output Cout
);

  wire alu_design_1_zero, and_1_out, Branch, N_F, not_1_out;
  wire [3:0] multiplexer_1_out;
  wire [11:0] adder_1_out, adder_2_out, adder_3_out, bit_extender_1_out, bit_extender_3_out,
       multiplexer_3_out, multiplexer_6_out, register_1_q, rom_1_data;
  wire [15:0] alu_design_1_alu_result, bit_extender_2_out, bit_extender_4_out, multiplexer_2_out,
       multiplexer_4_out, multiplexer_5_out, multiplexer_7_out, multiplexer_8_out, ram_1_dout,
       register_file_1_read_data_1, register_file_1_read_data_2, register_file_1_t0;

  Adder #(.width(12)) adder_1 (.a(register_1_q), .b(12'h1), .out(adder_1_out));  // open: cin, cout
  Register #(.width(12)) register_1 (.D(multiplexer_6_out), .en(Enable), .Q(register_1_q), .clk(Clock));  // open: clr
  ROM #(.addrWidth(12), .dataWidth(12)) rom_1 (.addr(register_1_q), .data(rom_1_data));
  Adder #(.width(12)) adder_2 (.a(adder_1_out), .b(bit_extender_1_out), .out(adder_2_out));  // open: cin, cout
  Multiplexer #(.width(4)) multiplexer_1 (.in0(rom_1_data[7:4]), .in1(4'b1000), .out(multiplexer_1_out), .sel(Slt_pin));
  Multiplexer #(.width(16)) multiplexer_2 (
    .in0(multiplexer_8_out), .in1(bit_extender_2_out), .out(multiplexer_2_out), .sel(Slt_pin));
  Multiplexer #(.width(12)) multiplexer_3 (.in0(adder_1_out), .in1(adder_2_out), .out(multiplexer_3_out), .sel(Branch));
  Register_File register_file_1 (
    .RD(multiplexer_1_out), .Input_Data(multiplexer_2_out), .Reg_Write_EN(Reg_WE), .Clock(Clock),
    .Read_Reg_2(rom_1_data[7:4]), .Read_Reg_1(rom_1_data[3:0]), .t0(register_file_1_t0),
    .Read_Data_1(register_file_1_read_data_1), .Read_Data_2(register_file_1_read_data_2));
  assign bit_extender_1_out = {{8{1'b0}}, rom_1_data[3:0]};  // Bit_Extender bit_extender_1
  assign bit_extender_2_out = {{15{1'b0}}, N_F};  // Bit_Extender bit_extender_2
  assign bit_extender_3_out = {{4{1'b0}}, rom_1_data[7:0]};  // Bit_Extender bit_extender_3
  assign bit_extender_4_out = {{12{1'b0}}, rom_1_data[3:0]};  // Bit_Extender bit_extender_4
  Multiplexer #(.width(16)) multiplexer_4 (
    .in0(register_file_1_read_data_1), .in1(bit_extender_4_out), .out(multiplexer_4_out), .sel(I_C));
  Multiplexer #(.width(16)) multiplexer_5 (
    .in0(register_file_1_read_data_2), .in1(register_file_1_t0), .out(multiplexer_5_out), .sel(t0_C));
  Multiplexer #(.width(12)) multiplexer_6 (
    .in0(multiplexer_3_out), .in1(adder_3_out), .out(multiplexer_6_out), .sel(Jump_pin));
  Adder #(.width(12)) adder_3 (.a(multiplexer_3_out), .b(bit_extender_3_out), .out(adder_3_out));  // open: cin, cout
  Multiplexer #(.width(16)) multiplexer_7 (
    .in0(multiplexer_4_out), .in1(register_file_1_read_data_2), .out(multiplexer_7_out), .sel(Branch_MP));
  RAM #(.addrWidth(16), .asyncread("true"), .dataWidth(16)) ram_1 (
    .addr(alu_design_1_alu_result), .we(S_E), .oe(L_E), .clk(Clock), .din(register_file_1_read_data_2),
    .dout(ram_1_dout));
  ALU_Design alu_design_1 (
    .Data_1(multiplexer_5_out), .Data_2(multiplexer_7_out), .ALU_OPcode(ALU_OPcode), .Invert(B_inv),
    .Cin(Cin), .ALU_Result(alu_design_1_alu_result), .ZerO(alu_design_1_zero), .Cout(Cout), .N_F(N_F));
  Multiplexer #(.width(16)) multiplexer_8 (
    .in0(alu_design_1_alu_result), .in1(ram_1_dout), .out(multiplexer_8_out), .sel(Load_Pin));
  and and_1 (and_1_out, alu_design_1_zero, Zero_C);
  Multiplexer multiplexer_9 (.in0(and_1_out), .in1(not_1_out), .out(Branch), .sel(bne_pin));
  not not_1 (not_1_out, alu_design_1_zero);

  // Other names for the same wires on the sheet: branch_pin = Branch_MP; default_reg = t0_C; I_pin = I_C;
  //   jump = Jump_pin; LW_EN = L_E; Mem_Clk = Clock; slt = Slt_pin; SW_EN = S_E; Zero_Signal = Zero_C

  // Notes on the sheet:
  //   contents of rom_1 (hex, n*v repeats v):
  //   456 5*0 6
endmodule

module sll_t (
  input  B_inv,
  input  Cin,
  input  Clock,
  input  [2:0] ALU_OPcode,
  input  Reg_WE,
  input  I_C,
  input  t0_C,
  input  Zero_C,
  input  Load_Pin,
  input  L_E,
  input  S_E,
  input  bne_pin,
  input  Branch_MP,
  input  Jump_pin,
  input  Slt_pin,
  input  sll_pin,
  input  dr_ac,
  output Cout
);

  wire alu_design_1_zero, and_1_out, Branch, N_F, not_1_out;
  wire [3:0] multiplexer_1_out;
  wire [11:0] adder_1_out, adder_2_out, adder_3_out, bit_extender_1_out, bit_extender_3_out,
       multiplexer_2_out, multiplexer_8_out, register_1_q, rom_1_data;
  wire [15:0] alu_design_1_alu_result, bit_extender_2_out, bit_extender_4_out, multiplexer_3_out,
       multiplexer_4_out, multiplexer_5_out, multiplexer_6_out, multiplexer_7_out, multiplexer_9_out,
       ram_1_dout, register_file_1_read_data_1, register_file_1_read_data_2, register_file_1_t0, shift_left;

  Adder #(.width(12)) adder_1 (.a(register_1_q), .b(12'h1), .out(adder_1_out));  // open: cin, cout
  Register #(.width(12)) register_1 (.D(multiplexer_8_out), .en(Clock), .Q(register_1_q), .clk(Clock));  // open: clr
  ROM #(.addrWidth(12), .dataWidth(12)) rom_1 (.addr(register_1_q), .data(rom_1_data));
  Adder #(.width(12)) adder_2 (.a(adder_1_out), .b(bit_extender_1_out), .out(adder_2_out));  // open: cin, cout
  Multiplexer #(.width(4)) multiplexer_1 (.in0(rom_1_data[7:4]), .in1(4'b1000), .out(multiplexer_1_out), .sel(dr_ac));
  Multiplexer #(.width(12)) multiplexer_2 (.in0(adder_1_out), .in1(adder_2_out), .out(multiplexer_2_out), .sel(Branch));
  Register_File register_file_1 (
    .RD(multiplexer_1_out), .Input_Data(multiplexer_3_out), .Reg_Write_EN(Reg_WE), .Clock(Clock),
    .Read_Reg_2(rom_1_data[7:4]), .Read_Reg_1(rom_1_data[3:0]), .t0(register_file_1_t0),
    .Read_Data_1(register_file_1_read_data_1), .Read_Data_2(register_file_1_read_data_2));
  Multiplexer #(.width(16)) multiplexer_3 (
    .in0(multiplexer_6_out), .in1(bit_extender_2_out), .out(multiplexer_3_out), .sel(Slt_pin));
  assign bit_extender_1_out = {{8{1'b0}}, rom_1_data[3:0]};  // Bit_Extender bit_extender_1
  assign bit_extender_2_out = {{15{1'b0}}, N_F};  // Bit_Extender bit_extender_2
  assign bit_extender_3_out = {{4{1'b0}}, rom_1_data[7:0]};  // Bit_Extender bit_extender_3
  assign bit_extender_4_out = {{12{1'b0}}, rom_1_data[3:0]};  // Bit_Extender bit_extender_4
  Multiplexer #(.width(16)) multiplexer_4 (
    .in0(register_file_1_read_data_1), .in1(bit_extender_4_out), .out(multiplexer_4_out), .sel(I_C));
  Multiplexer #(.width(16)) multiplexer_5 (
    .in0(register_file_1_read_data_2), .in1(register_file_1_t0), .out(multiplexer_5_out), .sel(t0_C));
  Multiplexer #(.width(16)) multiplexer_6 (
    .in0(multiplexer_9_out), .in1(shift_left), .out(multiplexer_6_out), .sel(sll_pin));
  RAM #(.addrWidth(16), .asyncread("true"), .dataWidth(16)) ram_1 (
    .addr(alu_design_1_alu_result), .we(S_E), .oe(L_E), .clk(Clock), .din(register_file_1_read_data_2),
    .dout(ram_1_dout));
  Adder #(.width(12)) adder_3 (.a(multiplexer_2_out), .b(bit_extender_3_out), .out(adder_3_out));  // open: cin, cout
  Shifter #(.width(16)) shifter_1 (.in(register_file_1_read_data_2), .\dist (rom_1_data[3:0]), .out(shift_left));
  Multiplexer #(.width(16)) multiplexer_7 (
    .in0(multiplexer_4_out), .in1(register_file_1_read_data_2), .out(multiplexer_7_out), .sel(Branch_MP));
  Multiplexer #(.width(12)) multiplexer_8 (
    .in0(multiplexer_2_out), .in1(adder_3_out), .out(multiplexer_8_out), .sel(Jump_pin));
  ALU_Design alu_design_1 (
    .Data_1(multiplexer_5_out), .Data_2(multiplexer_7_out), .ALU_OPcode(ALU_OPcode), .Invert(B_inv),
    .Cin(Cin), .ALU_Result(alu_design_1_alu_result), .ZerO(alu_design_1_zero), .Cout(Cout), .N_F(N_F));
  Multiplexer #(.width(16)) multiplexer_9 (
    .in0(alu_design_1_alu_result), .in1(ram_1_dout), .out(multiplexer_9_out), .sel(Load_Pin));
  and and_1 (and_1_out, alu_design_1_zero, Zero_C);
  Multiplexer multiplexer_10 (.in0(and_1_out), .in1(not_1_out), .out(Branch), .sel(bne_pin));
  not not_1 (not_1_out, alu_design_1_zero);

  // Other names for the same wires on the sheet: branch_pin = Branch_MP; default_reg = t0_C; I_pin = I_C;
  //   jump = Jump_pin; LW_EN = L_E; Mem_Clk = Clock; sll_p = sll_pin; slt = Slt_pin; SW_EN = S_E;
  //   Zero_Signal = Zero_C

  // Notes on the sheet:
  //   contents of rom_1 (hex, n*v repeats v):
  //   123 120 122 123 0 0 6
endmodule

module Control_New (
  input  [3:0] OP_Code,
  output [2:0] ALU_OP,
  output Bin,
  output Cin,
  output Reg_WE,
  output default_reg,
  output Zero_C,
  output Load_Pin,
  output LE,
  output SE,
  output bne,
  output Branch_Pin,
  output Jump,
  output Slt_pin,
  output sll_pin,
  output dr_ac,
  output I_pin
);

  wire and_1_out, and_2_out, and_3_out, and_4_out, and_5_out, and_6_out, and_7_out, and_8_out, and_9_out,
       and_10_out, and_11_out, and_12_out, and_13_out, and_14_out, and_15_out, and_16_out, and_17_out,
       and_18_out, and_19_out, and_20_out, and_21_out, and_22_out, and_29_out, and_30_out, and_32_out,
       and_33_out, and_34_out, and_35_out, and_36_out, and_37_out, not_1_out, not_2_out, not_3_out, not_4_out;

  not not_1 (not_1_out, OP_Code[3]);
  not not_2 (not_2_out, OP_Code[2]);
  not not_3 (not_3_out, OP_Code[1]);
  not not_4 (not_4_out, OP_Code[0]);
  and and_1 (and_1_out, OP_Code[3], not_2_out, not_3_out, not_4_out);
  and and_2 (and_2_out, not_1_out, OP_Code[2], OP_Code[0]);
  and and_3 (and_3_out, not_1_out, not_2_out);
  and and_4 (and_4_out, OP_Code[3], OP_Code[2]);
  and and_5 (and_5_out, not_2_out, OP_Code[0]);
  and and_6 (and_6_out, not_2_out, OP_Code[1]);
  and and_7 (and_7_out, OP_Code[1], not_4_out);
  and and_8 (and_8_out, not_1_out, not_2_out, OP_Code[1]);
  and and_9 (and_9_out, OP_Code[3], OP_Code[2]);
  and and_10 (and_10_out, not_2_out, OP_Code[1], OP_Code[0]);
  and and_11 (and_11_out, not_1_out, not_2_out, OP_Code[1]);
  and and_12 (and_12_out, OP_Code[3], OP_Code[2]);
  and and_13 (and_13_out, not_2_out, OP_Code[1], OP_Code[0]);
  and and_14 (and_14_out, not_2_out, not_3_out);
  and and_15 (and_15_out, not_3_out, OP_Code[0]);
  and and_16 (and_16_out, OP_Code[2], OP_Code[1], not_4_out);
  and and_17 (and_17_out, not_1_out, OP_Code[2], not_3_out, OP_Code[0]);
  and and_18 (and_18_out, OP_Code[3], not_2_out, OP_Code[0]);
  and and_19 (and_19_out, OP_Code[3], not_2_out, OP_Code[1]);
  and and_20 (and_20_out, OP_Code[3], OP_Code[2], not_3_out, not_4_out);
  and and_21 (and_21_out, OP_Code[3], not_2_out, OP_Code[1], OP_Code[0]);
  and and_22 (and_22_out, OP_Code[3], OP_Code[2], not_3_out);
  and and_23 (Load_Pin, OP_Code[3], not_2_out, not_3_out, OP_Code[0]);
  and and_24 (LE, OP_Code[3], not_2_out, not_3_out, OP_Code[0]);
  and and_25 (SE, OP_Code[3], not_2_out, OP_Code[1], not_4_out);
  and and_26 (bne, OP_Code[3], OP_Code[2], not_3_out, not_4_out);
  and and_27 (Branch_Pin, OP_Code[3], not_2_out, OP_Code[1], OP_Code[0]);
  and and_28 (Jump, OP_Code[3], OP_Code[2], OP_Code[1], OP_Code[0]);
  and and_29 (and_29_out, OP_Code[3], OP_Code[2], not_3_out, OP_Code[0]);
  and and_30 (and_30_out, OP_Code[3], OP_Code[2], OP_Code[1], not_4_out);
  and and_31 (sll_pin, not_1_out, OP_Code[2], not_3_out, OP_Code[0]);
  and and_32 (and_32_out, OP_Code[2], not_3_out, OP_Code[0]);
  and and_33 (and_33_out, OP_Code[3], OP_Code[2], OP_Code[1], not_4_out);
  and and_34 (and_34_out, not_2_out, OP_Code[0]);
  and and_35 (and_35_out, not_3_out, OP_Code[0]);
  and and_36 (and_36_out, OP_Code[3], OP_Code[1], not_4_out);
  and and_37 (and_37_out, OP_Code[3], OP_Code[2], not_4_out);
  or or_1 (ALU_OP[2], and_1_out, and_2_out);
  or or_2 (ALU_OP[1], and_3_out, and_4_out, and_5_out, and_6_out);
  or or_3 (ALU_OP[0], not_2_out, and_7_out, OP_Code[3]);
  or or_4 (Bin, and_8_out, and_9_out, and_10_out);
  or or_5 (Cin, and_11_out, and_12_out, and_13_out);
  or or_6 (Reg_WE, not_1_out, and_14_out, and_15_out, and_16_out);
  or or_7 (default_reg, and_17_out, and_18_out, and_19_out, and_20_out);
  or or_8 (Zero_C, and_21_out, and_22_out);
  or or_9 (Slt_pin, and_29_out, and_30_out);
  or or_10 (dr_ac, and_32_out, and_33_out);
  or or_11 (I_pin, and_34_out, and_35_out, and_36_out, and_37_out);
endmodule
